# Fritzing sketch design (saved by Fritzing 0.9.5d)
breadboards: 2

parts:
  U1 = ESP32S-HiLetgo [part_number=ESP32S-HiLetgo]
  IC1 = L293D [package=THT]
  tl = DC Motor
  br = DC Motor
  bl = DC Motor
  tr = DC Motor
  Part1 = NCP1400 Step-Up Breakout
  VCC1 = Battery
  BAT1 = 18650 battery holder [package=battery-18650-kit]
  U2 = ESP32S-HiLetgo [part_number=ESP32S-HiLetgo]
  Part2 = Thumb Joystick

nets:
  GND: U1.GND, IC1.0V, Part1.GND, BAT1.-
  N1: U1.VIN, IC1.Enable_1, IC1.Enable_2, IC1.+V, Part1.VOUT
  N2: U1.GPIO5, IC1.In_4
  N3: U1.GPIO18, IC1.In_3
  N4: U1.GPIO19, IC1.In_2
  N5: U1.GPIO21, IC1.In_1
  N6: IC1.Out_1_(_Controlled_by_Enable_1_), tl.pin_1, bl.pin_1
  N7: IC1.Out_2_(_Controlled_by_Enable_1_), tl.pin_2, bl.pin_2
  N8: IC1.+Vmotor, Part1.VIN, VCC1.+
  N9: IC1.Out_3_(_Controlled_by_Enable_2_), br.pin_1, tr.pin_1
  N10: IC1.Out_4_(_Controlled_by_Enable_2_), br.pin_2, tr.pin_2
  N11: VCC1.-, BAT1.+
  N12: U2.3.3, Part2.VCC
  GND_2: U2.GND, Part2.GND
  N13: U2.GPIO2, Part2.HORZ
  N14: U2.GPIO4, Part2.VERT

custom parts:
  ESP32S-HiLetgo: HiLetgo ESP-WROOM-32 ESP32 ESP-32S Development Board 2.4GHz Dual-Mode WiFi + Bluetooth Dual Cores Microcontroller The ESP32 integrated with Antenna switches, RF Balun, power amplifiers, low-noise amplifiers, filters, and management modules, and the entire solution occupies the least area of PCB. 2.4 GHz Wi-Fi plus Bluetooth dual-mode chip, with TSMC Ultra-low power consumption 40nm technology,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
  Battery: Your standard 2x 18650 battery pack (7,4 Volts)
  18650 battery holder: 18650 Battery Holder identical to the dual battery version.
